// Logisim project ADD_4.circ as structural Verilog
module ADD_1 (
  input  A,
  input  B,
  input  C,
  output \Saída ,
  output Vai_1
);

  wire and_1_out, and_2_out, or_1_out, xor_1_out;

  xor xor_1 (xor_1_out, C, B);
  or or_1 (or_1_out, C, B);
  and and_1 (and_1_out, B, C);
  xor xor_2 (\Saída , xor_1_out, A);
  and and_2 (and_2_out, or_1_out, A);
  or or_2 (Vai_1, and_2_out, and_1_out);
endmodule

module ADD_4 (
  input  [3:0] B,
  input  [3:0] A,
  input  Vem_1,
  output Vai_1,
  output [3:0] out_5
);

  wire add_1_2_vai_1, add_1_3_vai_1, add_1_4_vai_1;

  ADD_1 add_1_1 (.\Saída (out_5[3]), .Vai_1(Vai_1), .A(A[3]), .B(B[3]), .C(add_1_2_vai_1));
  ADD_1 add_1_2 (.\Saída (out_5[2]), .Vai_1(add_1_2_vai_1), .A(A[2]), .B(B[2]), .C(add_1_3_vai_1));
  ADD_1 add_1_3 (.\Saída (out_5[1]), .Vai_1(add_1_3_vai_1), .A(A[1]), .B(B[1]), .C(add_1_4_vai_1));
  // Probe on out_5
  ADD_1 add_1_4 (.\Saída (out_5[0]), .Vai_1(add_1_4_vai_1), .A(A[0]), .B(B[0]), .C(Vem_1));
endmodule
